# Fritzing sketch fsm_automatic_door (saved by Fritzing 0.9.3b)
breadboards: 1

parts:
  J2 = STM32 Nucleo boards
  Part1 = HC-SR501 Body Sensor Module
  LED3 = RGB LED (com. cathode, rbg) [package="5 mm [THT]"]
  R6 = Resistor [tolerance=±5% resistance=91 package=THT]
  R7 = Resistor [tolerance=±5% resistance=150 package="0603 [SMD]"]

nets:
  N1: J2.D10_PWM/SS, R7.Pin_0
  N2: J2.A4/SDA, R6.Pin_0
  N3: J2.D2, Part1.OUT
  5V: J2.5V, Part1.VCC
  GND: J2.GND, Part1.GND, LED3.common_cathode
  N4: LED3.red_anode, R7.Pin_1
  N5: LED3.blue_anode, R6.Pin_1

custom parts:
  HC-SR501 Body Sensor Module: Pyroelectric Infrared PIR Motion Sensor Detector Module
